# Fritzing sketch esquema_frit (saved by Fritzing 0.9.3b)
breadboards: 1

parts:
  R1 = Resistor [tolerance=±5% resistance=220 package=THT]
  LED1 = LED - 5mm [color="Red (633nm)" package="5 mm [THT]"]
  R2 = Resistor [tolerance=±5% resistance=220 package=THT]
  LED2 = LED - 5mm [color="Red (633nm)" package="5 mm [THT]"]
  Componente1 = Arduino Uno (Rev3)

nets:
  N1: R1.Pin_0, LED1.anode
  N2: R1.Pin_1, Componente1.D8
  N3: LED1.cathode, LED2.anode, Componente1.GND
  N4: R2.Pin_0, Componente1.D9_PWM
  N5: R2.Pin_1, LED2.cathode
